// Logisim project ex2.circ as structural Verilog: 1 circuit, main circuit compute_BrUn
module compute_BrUn (
  input  [31:0] INSTRUCTION,
  output BrUn
);

  wire comparator_1_eq, comparator_1_gt, comparator_1_lt, not_1_out, or_1_out;

  Comparator #(.width(3)) comparator_1 (
    .a(INSTRUCTION[14:12]), .b(3'b110), .gt(comparator_1_gt), .eq(comparator_1_eq), .lt(comparator_1_lt));
  not not_1 (not_1_out, comparator_1_lt);
  or or_1 (or_1_out, comparator_1_gt, comparator_1_eq);
  and and_1 (BrUn, or_1_out, not_1_out);
endmodule
