// Logisim project branch-comp.circ as structural Verilog: 1 circuit, main circuit branch_comp
module branch_comp (
  input  [31:0] BrData1,
  input  [31:0] BrData2,
  input  BrUn,
  output BrEq,
  output BrLt
);

  wire BrEq0, BrEq1, BrLt0, BrLt1;

  Comparator #(.width(32)) comparator_1 (.a(BrData1), .b(BrData2), .eq(BrEq0), .lt(BrLt0));  // open: gt
  Comparator #(.mode("unsigned"), .width(32)) comparator_2 (
    .a(BrData1), .b(BrData2), .eq(BrEq1), .lt(BrLt1));  // open: gt
  Multiplexer multiplexer_1 (.in0(BrEq0), .in1(BrEq1), .out(BrEq), .sel(BrUn));
  Multiplexer multiplexer_2 (.in0(BrLt0), .in1(BrLt1), .out(BrLt), .sel(BrUn));

  // Notes on the sheet:
  //   INPUTS to your circuit
  //   DON'T CHANGE THE LOCATIONS OF THE INPUTS AND OUTPUTS!
  //   OUTPUT from your circuit
endmodule
