// Logisim project control-logic.circ as structural Verilog: 1 circuit, main circuit control_logic
module control_logic (
  input  [31:0] Instruction,
  input  BrEq,
  input  BrLt,
  output PCSel,
  output RegWEn,
  output [2:0] ImmSel,
  output BrUn,
  output ASel,
  output BSel,
  output [3:0] ALUSel,
  output MemWEn,
  output [1:0] WBSel
);

  wire and_1_out, and_2_out, and_3_out, and_4_out, and_5_out, and_6_out, and_7_out, and_8_out, and_9_out,
       and_10_out, BType, comparator_10_eq, comparator_11_eq, comparator_12_eq, comparator_21_eq, IsAdd,
       IsAddi, IsAnd, IsAndi, IsAuipc, IsBeq, IsBge, IsBgeu, IsBlt, IsBltu, IsBne, IsJal, IsJalr, IsLb, IsLh,
       IsLui, IsLw, IsMul, IsMulh, IsMulhu, IsOr, IsOri, IsSb, IsSh, IsSll, IsSlli, IsSlt, IsSlti, IsSra,
       IsSrai, IsSrl, IsSrli, IsSub, IsSw, IsXor, IsXori, IType, LoadType, not_1_out, not_2_out, not_3_out,
       not_4_out, not_5_out, not_6_out, not_7_out, or_1_out, or_2_out, or_3_out, or_4_out, or_5_out, RType,
       StoreType;
  wire [1:0] priority_encoder_1_out;
  wire [5:0] BTypeInstruction, ITypeInstruction, LoadTypeInstruction, multiplexer_1_out, multiplexer_2_out,
       multiplexer_3_out, multiplexer_4_out, RomInput, RTypeInstruction, StoreTypeInstruction;
  wire [15:14] rom_1_data;

  ROM #(.addrWidth(6), .dataWidth(16)) rom_1 (
    .addr(RomInput), .data({rom_1_data, WBSel, MemWEn, ALUSel, BSel, ASel, BrUn, ImmSel, RegWEn}));
  Comparator #(.width(7)) comparator_1 (.a(Instruction[6:0]), .b(7'b0010011), .eq(IType));  // open: gt, lt
  Comparator #(.width(7)) comparator_2 (.a(Instruction[6:0]), .b(7'b0110011), .eq(RType));  // open: gt, lt
  Comparator #(.width(7)) comparator_3 (.a(Instruction[6:0]), .b(7'b1100011), .eq(BType));  // open: gt, lt
  Comparator #(.width(7)) comparator_4 (.a(Instruction[6:0]), .b(7'b0000011), .eq(LoadType));  // open: gt, lt
  Comparator #(.width(7)) comparator_5 (.a(Instruction[6:0]), .b(7'b0100011), .eq(StoreType));  // open: gt, lt
  Comparator #(.width(7)) comparator_6 (.a(Instruction[6:0]), .b(7'b0010111), .eq(IsAuipc));  // open: gt, lt
  Comparator #(.width(7)) comparator_7 (.a(Instruction[6:0]), .b(7'b0110111), .eq(IsLui));  // open: gt, lt
  Comparator #(.width(7)) comparator_8 (.a(Instruction[6:0]), .b(7'b1101111), .eq(IsJal));  // open: gt, lt
  Comparator #(.width(7)) comparator_9 (.a(Instruction[6:0]), .b(7'b1100111), .eq(IsJalr));  // open: gt, lt
  Comparator #(.width(7)) comparator_10 (.a(Instruction[31:25]), .b({7{1'b0}}), .eq(comparator_10_eq));  // open: gt, lt
  Comparator #(.width(7)) comparator_11 (
    .a(Instruction[31:25]), .b(7'b0000001), .eq(comparator_11_eq));  // open: gt, lt
  Comparator #(.width(7)) comparator_12 (
    .a(Instruction[31:25]), .b(7'b0100000), .eq(comparator_12_eq));  // open: gt, lt
  Multiplexer #(.enable("true"), .width(6)) multiplexer_1 (
    .in0(6'b010011), .in1(6'b010100), .out(multiplexer_1_out), .sel(Instruction[30]), .en(IType));
  Priority_Encoder #(.select_enc(2)) priority_encoder_1 (
    .in0(comparator_10_eq), .in1(comparator_11_eq), .in2(comparator_12_eq), .in3(1'b0),
    .out(priority_encoder_1_out));  // open: gs, en_out, en_in
  Multiplexer #(.enable("true"), .width(6)) multiplexer_2 (
    .in0(6'b000011), .in1(6'b000100), .out(multiplexer_2_out), .sel(Instruction[25]), .en(RType));
  Multiplexer #(.enable("true"), .width(6)) multiplexer_3 (
    .in0(6'b001000), .in1(6'b001001), .out(multiplexer_3_out), .sel(Instruction[30]), .en(RType));
  Multiplexer #(.enable("true"), .select(2), .width(6)) multiplexer_4 (
    .in0({6{1'b0}}), .in1(6'b000001), .in2(6'b000010), .in3({6{1'b1}}), .out(multiplexer_4_out),
    .sel(priority_encoder_1_out), .en(RType));
  Multiplexer #(.enable("true"), .select(3), .width(6)) multiplexer_5 (
    .in0(6'b001111), .in1(6'b010000), .in2(6'b010001), .in3({6{1'b0}}), .in4(6'b010010),
    .in5(multiplexer_1_out), .in6(6'b010101), .in7(6'b010110), .out(ITypeInstruction),
    .sel(Instruction[14:12]), .en(IType));
  Multiplexer #(.enable("true"), .select(3), .width(6)) multiplexer_6 (
    .in0(6'b011010), .in1(6'b011011), .in2({6{1'b1}}), .in3({6{1'b1}}), .in4(6'b011100), .in5(6'b011101),
    .in6(6'b011110), .in7(6'b011111), .out(BTypeInstruction), .sel(Instruction[14:12]), .en(BType));
  Multiplexer #(.enable("true"), .select(2), .width(6)) multiplexer_7 (
    .in0(6'b001100), .in1(6'b001101), .in2(6'b001110), .in3({6{1'b1}}), .out(LoadTypeInstruction),
    .sel(Instruction[13:12]), .en(LoadType));
  Multiplexer #(.enable("true"), .select(2), .width(6)) multiplexer_8 (
    .in0(6'b010111), .in1(6'b011000), .in2(6'b011001), .in3({6{1'b1}}), .out(StoreTypeInstruction),
    .sel(Instruction[13:12]), .en(StoreType));
  not not_1 (not_1_out, BrEq);
  not not_2 (not_2_out, BrLt);
  not not_3 (not_3_out, BrLt);
  Multiplexer #(.enable("true"), .select(3), .width(6)) multiplexer_9 (
    .in0(multiplexer_4_out), .in1(multiplexer_2_out), .in2(6'b000110), .in3(6'b000101), .in4(6'b000111),
    .in5(multiplexer_3_out), .in6(6'b001010), .in7(6'b001011), .out(RTypeInstruction),
    .sel(Instruction[14:12]), .en(RType));
  and and_1 (and_1_out, IsBeq, BrEq);
  and and_2 (and_2_out, IsBne, not_1_out);
  not not_4 (not_4_out, IsBlt);
  not not_5 (not_5_out, and_9_out);
  and and_3 (and_3_out, IsBlt, BrLt);
  and and_4 (and_4_out, IsBge, not_2_out);
  not not_6 (not_6_out, BrEq);
  and and_5 (and_5_out, IsBltu, BrLt);
  and and_6 (and_6_out, IsBgeu, not_3_out);
  not not_7 (not_7_out, BrEq);
  or or_1 (or_1_out, and_1_out, and_8_out);
  and and_7 (and_7_out, and_2_out, not_4_out);
  and and_8 (and_8_out, and_7_out, not_5_out);
  and and_9 (and_9_out, and_4_out, not_6_out);
  or or_2 (or_2_out, and_5_out, and_10_out);
  and and_10 (and_10_out, and_6_out, not_7_out);
  or or_3 (or_3_out, and_3_out, and_9_out);
  or or_4 (or_4_out, or_3_out, or_2_out);
  or or_5 (or_5_out, or_1_out, or_4_out);
  Multiplexer multiplexer_10 (.in0(1'b0), .in1(1'b1), .out(PCSel), .sel(or_5_out));
  Priority_Encoder #(.select_enc(6)) priority_encoder_2 (
    .in0(IsAdd), .in1(IsMul), .in2(IsSub), .in3(IsSll), .in4(IsMulh), .in5(IsMulhu), .in6(IsSlt),
    .in7(IsXor), .in8(IsSrl), .in9(IsSra), .in10(IsOr), .in11(IsAnd), .in12(IsLb), .in13(IsLh), .in14(IsLw),
    .in15(IsAddi), .in16(IsSlli), .in17(IsSlti), .in18(IsXori), .in19(IsSrli), .in20(IsSrai), .in21(IsOri),
    .in22(IsAndi), .in23(IsSb), .in24(IsSh), .in25(IsSw), .in26(IsBeq), .in27(IsBne), .in28(IsBlt),
    .in29(IsBge), .in30(IsBltu), .in31(IsBgeu), .in32(IsAuipc), .in33(IsLui), .in34(IsJal), .in35(IsJalr),
    .out(RomInput));  // open: in36, in37, in38, in39, in40, in41, in42, in43, in44, in45, in46, in47, in48, in49, in50, in51, in52, in53, in54, in55, in56, in57, in58, in59, in60, in61, in62, in63, gs, en_out, en_in
  Comparator #(.width(6)) comparator_13 (.a(ITypeInstruction), .b(6'b001111), .eq(IsAddi));  // open: gt, lt
  Comparator #(.width(6)) comparator_14 (.a(ITypeInstruction), .b(6'b010000), .eq(IsSlli));  // open: gt, lt
  Comparator #(.width(6)) comparator_15 (.a(ITypeInstruction), .b(6'b010001), .eq(IsSlti));  // open: gt, lt
  Comparator #(.width(6)) comparator_16 (.a(ITypeInstruction), .b(6'b010010), .eq(IsXori));  // open: gt, lt
  Comparator #(.width(6)) comparator_17 (.a(ITypeInstruction), .b(6'b010011), .eq(IsSrli));  // open: gt, lt
  Comparator #(.width(6)) comparator_18 (.a(ITypeInstruction), .b(6'b010100), .eq(IsSrai));  // open: gt, lt
  Comparator #(.width(6)) comparator_19 (.a(ITypeInstruction), .b(6'b010101), .eq(IsOri));  // open: gt, lt
  Comparator #(.width(6)) comparator_20 (.a(ITypeInstruction), .b(6'b010110), .eq(IsAndi));  // open: gt, lt
  Comparator #(.width(6)) comparator_21 (.a(RTypeInstruction), .b({6{1'b0}}), .eq(comparator_21_eq));  // open: gt, lt
  Comparator #(.width(6)) comparator_22 (.a(RTypeInstruction), .b(6'b000001), .eq(IsMul));  // open: gt, lt
  Comparator #(.width(6)) comparator_23 (.a(RTypeInstruction), .b(6'b000010), .eq(IsSub));  // open: gt, lt
  Comparator #(.width(6)) comparator_24 (.a(RTypeInstruction), .b(6'b000011), .eq(IsSll));  // open: gt, lt
  Comparator #(.width(6)) comparator_25 (.a(RTypeInstruction), .b(6'b000100), .eq(IsMulh));  // open: gt, lt
  Comparator #(.width(6)) comparator_26 (.a(RTypeInstruction), .b(6'b000101), .eq(IsMulhu));  // open: gt, lt
  Comparator #(.width(6)) comparator_27 (.a(RTypeInstruction), .b(6'b000110), .eq(IsSlt));  // open: gt, lt
  Comparator #(.width(6)) comparator_28 (.a(RTypeInstruction), .b(6'b000111), .eq(IsXor));  // open: gt, lt
  Comparator #(.width(6)) comparator_29 (.a(RTypeInstruction), .b(6'b001000), .eq(IsSrl));  // open: gt, lt
  Comparator #(.width(6)) comparator_30 (.a(RTypeInstruction), .b(6'b001001), .eq(IsSra));  // open: gt, lt
  Comparator #(.width(6)) comparator_31 (.a(RTypeInstruction), .b(6'b001010), .eq(IsOr));  // open: gt, lt
  Comparator #(.width(6)) comparator_32 (.a(RTypeInstruction), .b(6'b001011), .eq(IsAnd));  // open: gt, lt
  Comparator #(.width(6)) comparator_33 (.a(BTypeInstruction), .b(6'b011010), .eq(IsBeq));  // open: gt, lt
  Comparator #(.width(6)) comparator_34 (.a(BTypeInstruction), .b(6'b011011), .eq(IsBne));  // open: gt, lt
  Comparator #(.width(6)) comparator_35 (.a(BTypeInstruction), .b(6'b011100), .eq(IsBlt));  // open: gt, lt
  Comparator #(.width(6)) comparator_36 (.a(BTypeInstruction), .b(6'b011101), .eq(IsBge));  // open: gt, lt
  Comparator #(.width(6)) comparator_37 (.a(BTypeInstruction), .b(6'b011110), .eq(IsBltu));  // open: gt, lt
  Comparator #(.width(6)) comparator_38 (.a(BTypeInstruction), .b(6'b011111), .eq(IsBgeu));  // open: gt, lt
  Comparator #(.width(6)) comparator_39 (.a(LoadTypeInstruction), .b(6'b001100), .eq(IsLb));  // open: gt, lt
  Comparator #(.width(6)) comparator_40 (.a(LoadTypeInstruction), .b(6'b001101), .eq(IsLh));  // open: gt, lt
  Comparator #(.width(6)) comparator_41 (.a(LoadTypeInstruction), .b(6'b001110), .eq(IsLw));  // open: gt, lt
  Comparator #(.width(6)) comparator_42 (.a(StoreTypeInstruction), .b(6'b010111), .eq(IsSb));  // open: gt, lt
  Comparator #(.width(6)) comparator_43 (.a(StoreTypeInstruction), .b(6'b011000), .eq(IsSh));  // open: gt, lt
  Comparator #(.width(6)) comparator_44 (.a(StoreTypeInstruction), .b(6'b011001), .eq(IsSw));  // open: gt, lt
  and and_11 (IsAdd, comparator_21_eq, RType);

  // Other names for the same wires on the sheet: BTypeFun3[2:0] = Instruction[14:12];
  //   ITypeFun3[2:0] = Instruction[14:12]; LoadTypeFun3[2:0] = Instruction[14:12];
  //   RTypeFun3[2:0] = Instruction[14:12]; StoreTypeFun3[2:0] = Instruction[14:12];
  //   ITypeFun7[6:0] = Instruction[31:25]; RTypeFun7[6:0] = Instruction[31:25]

  // Notes on the sheet:
  //   INPUTS to your circuit
  //   Connect ROM Input here ->
  //   contents of rom_1 (hex, n*v repeats v):
  //   100f 140f 160f 109f 148f 159f 110f 121f 129f 168f 131f 139f 2051 2051 2051 1041 10d1 1141 1251 12d1
  //   16c1 1351 13d1 852 852 852 74 74 64 64 74 74 1077 17d7 3079 3051
  //   ROM FOR CONTROL LOGIC
  //   DON'T CHANGE THE LOCATIONS OF THE INPUTS AND OUTPUTS!
  //   This is only if you choose to do the ROM option
  //   CONNECT
  //   WIRE
  //   TO
  //   USE
  //   ROM
  //   OUTPUT from your circuit
  //   Reminder: If using ROM, use combinational logic for PCSel
endmodule
