// Logisim project partial-store.circ as structural Verilog: 1 circuit, main circuit partial_store
module partial_store (
  input  [31:0] Instruction,
  input  [31:0] MemAddress,
  input  [31:0] DataFromReg,
  input  MemRW,
  output [3:0] MemWriteMask,
  output [31:0] DataToMem
);

  wire and_1_out, and_2_out, and_3_out, and_4_out, and_5_out, and_6_out, and_7_out, comparator_1_eq,
       comparator_2_eq, comparator_3_eq, comparator_4_eq, comparator_5_eq, comparator_6_eq, comparator_7_eq,
       comparator_8_eq, not_1_out;
  wire [2:0] priority_encoder_1_out;
  wire [31:0] multiplexer_1_out, multiplexer_2_out;

  Comparator #(.width(3)) comparator_1 (.a(Instruction[14:12]), .b(3'b000), .eq(comparator_1_eq));  // open: gt, lt
  Comparator #(.width(3)) comparator_2 (.a(Instruction[14:12]), .b(3'b001), .eq(comparator_2_eq));  // open: gt, lt
  Comparator #(.width(3)) comparator_3 (.a(Instruction[14:12]), .b(3'b010), .eq(comparator_3_eq));  // open: gt, lt
  Comparator #(.width(2)) comparator_4 (.a(MemAddress[1:0]), .b(2'b00), .eq(comparator_4_eq));  // open: gt, lt
  Comparator #(.width(2)) comparator_5 (.a(MemAddress[1:0]), .b(2'b01), .eq(comparator_5_eq));  // open: gt, lt
  Comparator #(.width(2)) comparator_6 (.a(MemAddress[1:0]), .b(2'b10), .eq(comparator_6_eq));  // open: gt, lt
  Comparator #(.width(2)) comparator_7 (.a(MemAddress[1:0]), .b(2'b11), .eq(comparator_7_eq));  // open: gt, lt
  Multiplexer #(.select(2), .width(32)) multiplexer_1 (
    .in0({{24{1'b0}}, DataFromReg[7:0]}), .in1({{16{1'b0}}, DataFromReg[15:8], {8{1'b0}}}),
    .in2({{8{1'b0}}, DataFromReg[23:16], {16{1'b0}}}), .in3({DataFromReg[31:24], {24{1'b0}}}),
    .out(multiplexer_1_out), .sel(MemAddress[1:0]));
  Multiplexer #(.select(2), .width(32)) multiplexer_2 (
    .in0({{16{1'b0}}, DataFromReg[15:0]}), .in1({32{1'b1}}), .in2({DataFromReg[31:16], {16{1'b0}}}),
    .in3({32{1'b1}}), .out(multiplexer_2_out), .sel(MemAddress[1:0]));
  and and_1 (and_1_out, comparator_4_eq, comparator_1_eq);
  and and_2 (and_2_out, comparator_5_eq, comparator_1_eq);
  and and_3 (and_3_out, comparator_6_eq, comparator_1_eq);
  and and_4 (and_4_out, comparator_7_eq, comparator_1_eq);
  and and_5 (and_5_out, comparator_4_eq, comparator_2_eq);
  and and_6 (and_6_out, comparator_6_eq, comparator_2_eq);
  not not_1 (not_1_out, MemRW);
  and and_7 (and_7_out, and_1_out, MemRW);
  Priority_Encoder priority_encoder_1 (
    .in0(and_7_out), .in1(and_2_out), .in2(and_3_out), .in3(and_4_out), .in4(and_5_out), .in5(and_6_out),
    .in6(comparator_3_eq), .in7(not_1_out), .out(priority_encoder_1_out));  // open: en_in, gs, en_out
  Multiplexer #(.enable("true"), .select(2), .width(32)) multiplexer_3 (
    .in0(multiplexer_1_out), .in1(multiplexer_2_out), .in2(DataFromReg), .in3({32{1'b1}}), .out(DataToMem),
    .sel(Instruction[13:12]), .en(comparator_8_eq));
  Comparator #(.width(7)) comparator_8 (.a(Instruction[6:0]), .b(7'b0100011), .eq(comparator_8_eq));  // open: gt, lt
  Multiplexer #(.select(3), .width(4)) multiplexer_4 (
    .in0(4'b0001), .in1(4'b0010), .in2(4'b0100), .in3(4'b1000), .in4(4'b0011), .in5(4'b1100), .in6(4'b1111),
    .in7(4'b0000), .out(MemWriteMask), .sel(priority_encoder_1_out));

  // Other names for the same wires on the sheet: Opcode[6:0] = Instruction[6:0]; Fun3[2:0] = Instruction[14:12]

  // Notes on the sheet:
  //   INPUTS to your circuit
  //   DON'T CHANGE THE LOCATIONS OF THE INPUTS AND OUTPUTS!
  //   OUTPUT from your circuit
endmodule
