// Logisim project regfile.circ as structural Verilog: 1 circuit, main circuit regfile
module regfile (
  input  [4:0] ReadIndex1,
  input  [4:0] ReadIndex2,
  input  [4:0] WriteIndex,
  input  [31:0] WriteData,
  input  RegWEn,
  input  clk,
  output [31:0] ra,
  output [31:0] sp,
  output [31:0] t0,
  output [31:0] t1,
  output [31:0] t2,
  output [31:0] s0,
  output [31:0] s1,
  output [31:0] a0,
  output [31:0] ReadData1,
  output [31:0] ReadData2
);

  wire RegWEn1, RegWEn2, RegWEn3, RegWEn4, RegWEn5, RegWEn6, RegWEn7, RegWEn8, RegWEn9, RegWEn10, RegWEn11,
       RegWEn12, RegWEn13, RegWEn14, RegWEn15, RegWEn16, RegWEn17, RegWEn18, RegWEn19, RegWEn20, RegWEn21,
       RegWEn22, RegWEn23, RegWEn24, RegWEn25, RegWEn26, RegWEn27, RegWEn28, RegWEn29, RegWEn30, RegWEn31;
  wire [31:0] a1, a2, a3, a4, a5, a6, a7, data1, data2, data3, data4, data5, data6, data7, data8, data9,
       data10, data11, data12, data13, data14, data15, data16, data17, data18, data19, data20, data21,
       data22, data23, data24, data25, data26, data27, data28, data29, data30, data31, gp, s2, s3, s4, s5,
       s6, s7, s8, s9, s10, s11, t3, t4, t5, t6, tp, zero;

  Multiplexer #(.select(5)) multiplexer_1 (
    .in0(1'b0), .in1(RegWEn), .in2(1'b0), .in3(1'b0), .in4(1'b0), .in5(1'b0), .in6(1'b0), .in7(1'b0),
    .in8(1'b0), .in9(1'b0), .in10(1'b0), .in11(1'b0), .in12(1'b0), .in13(1'b0), .in14(1'b0), .in15(1'b0),
    .in16(1'b0), .in17(1'b0), .in18(1'b0), .in19(1'b0), .in20(1'b0), .in21(1'b0), .in22(1'b0), .in23(1'b0),
    .in24(1'b0), .in25(1'b0), .in26(1'b0), .in27(1'b0), .in28(1'b0), .in29(1'b0), .in30(1'b0), .in31(1'b0),
    .out(RegWEn1), .sel(WriteIndex));
  Multiplexer #(.select(5)) multiplexer_2 (
    .in0(1'b0), .in1(1'b0), .in2(RegWEn), .in3(1'b0), .in4(1'b0), .in5(1'b0), .in6(1'b0), .in7(1'b0),
    .in8(1'b0), .in9(1'b0), .in10(1'b0), .in11(1'b0), .in12(1'b0), .in13(1'b0), .in14(1'b0), .in15(1'b0),
    .in16(1'b0), .in17(1'b0), .in18(1'b0), .in19(1'b0), .in20(1'b0), .in21(1'b0), .in22(1'b0), .in23(1'b0),
    .in24(1'b0), .in25(1'b0), .in26(1'b0), .in27(1'b0), .in28(1'b0), .in29(1'b0), .in30(1'b0), .in31(1'b0),
    .out(RegWEn2), .sel(WriteIndex));
  Multiplexer #(.select(5)) multiplexer_3 (
    .in0(1'b0), .in1(1'b0), .in2(1'b0), .in3(RegWEn), .in4(1'b0), .in5(1'b0), .in6(1'b0), .in7(1'b0),
    .in8(1'b0), .in9(1'b0), .in10(1'b0), .in11(1'b0), .in12(1'b0), .in13(1'b0), .in14(1'b0), .in15(1'b0),
    .in16(1'b0), .in17(1'b0), .in18(1'b0), .in19(1'b0), .in20(1'b0), .in21(1'b0), .in22(1'b0), .in23(1'b0),
    .in24(1'b0), .in25(1'b0), .in26(1'b0), .in27(1'b0), .in28(1'b0), .in29(1'b0), .in30(1'b0), .in31(1'b0),
    .out(RegWEn3), .sel(WriteIndex));
  Multiplexer #(.select(5)) multiplexer_4 (
    .in0(1'b0), .in1(1'b0), .in2(1'b0), .in3(1'b0), .in4(RegWEn), .in5(1'b0), .in6(1'b0), .in7(1'b0),
    .in8(1'b0), .in9(1'b0), .in10(1'b0), .in11(1'b0), .in12(1'b0), .in13(1'b0), .in14(1'b0), .in15(1'b0),
    .in16(1'b0), .in17(1'b0), .in18(1'b0), .in19(1'b0), .in20(1'b0), .in21(1'b0), .in22(1'b0), .in23(1'b0),
    .in24(1'b0), .in25(1'b0), .in26(1'b0), .in27(1'b0), .in28(1'b0), .in29(1'b0), .in30(1'b0), .in31(1'b0),
    .out(RegWEn4), .sel(WriteIndex));
  Multiplexer #(.select(5), .width(32)) multiplexer_5 (
    .in1(WriteData), .out(data1), .sel(WriteIndex));  // open: in0, in2, in3, in4, in5, in6, in7, in8, in9, in10, in11, in12, in13, in14, in15, in16, in17, in18, in19, in20, in21, in22, in23, in24, in25, in26, in27, in28, in29, in30, in31
  Multiplexer #(.select(5), .width(32)) multiplexer_6 (
    .in2(WriteData), .out(data2), .sel(WriteIndex));  // open: in0, in1, in3, in4, in5, in6, in7, in8, in9, in10, in11, in12, in13, in14, in15, in16, in17, in18, in19, in20, in21, in22, in23, in24, in25, in26, in27, in28, in29, in30, in31
  Multiplexer #(.select(5), .width(32)) multiplexer_7 (
    .in3(WriteData), .out(data3), .sel(WriteIndex));  // open: in0, in1, in2, in4, in5, in6, in7, in8, in9, in10, in11, in12, in13, in14, in15, in16, in17, in18, in19, in20, in21, in22, in23, in24, in25, in26, in27, in28, in29, in30, in31
  Multiplexer #(.select(5), .width(32)) multiplexer_8 (
    .in4(WriteData), .out(data4), .sel(WriteIndex));  // open: in0, in1, in2, in3, in5, in6, in7, in8, in9, in10, in11, in12, in13, in14, in15, in16, in17, in18, in19, in20, in21, in22, in23, in24, in25, in26, in27, in28, in29, in30, in31
  Multiplexer #(.select(5), .width(32)) multiplexer_9 (
    .in5(WriteData), .out(data5), .sel(WriteIndex));  // open: in0, in1, in2, in3, in4, in6, in7, in8, in9, in10, in11, in12, in13, in14, in15, in16, in17, in18, in19, in20, in21, in22, in23, in24, in25, in26, in27, in28, in29, in30, in31
  Multiplexer #(.select(5), .width(32)) multiplexer_10 (
    .in6(WriteData), .out(data6), .sel(WriteIndex));  // open: in0, in1, in2, in3, in4, in5, in7, in8, in9, in10, in11, in12, in13, in14, in15, in16, in17, in18, in19, in20, in21, in22, in23, in24, in25, in26, in27, in28, in29, in30, in31
  Multiplexer #(.select(5), .width(32)) multiplexer_11 (
    .in7(WriteData), .out(data7), .sel(WriteIndex));  // open: in0, in1, in2, in3, in4, in5, in6, in8, in9, in10, in11, in12, in13, in14, in15, in16, in17, in18, in19, in20, in21, in22, in23, in24, in25, in26, in27, in28, in29, in30, in31
  Multiplexer #(.select(5), .width(32)) multiplexer_12 (
    .in8(WriteData), .out(data8), .sel(WriteIndex));  // open: in0, in1, in2, in3, in4, in5, in6, in7, in9, in10, in11, in12, in13, in14, in15, in16, in17, in18, in19, in20, in21, in22, in23, in24, in25, in26, in27, in28, in29, in30, in31
  Multiplexer #(.select(5)) multiplexer_13 (
    .in0(1'b0), .in1(1'b0), .in2(1'b0), .in3(1'b0), .in4(1'b0), .in5(RegWEn), .in6(1'b0), .in7(1'b0),
    .in8(1'b0), .in9(1'b0), .in10(1'b0), .in11(1'b0), .in12(1'b0), .in13(1'b0), .in14(1'b0), .in15(1'b0),
    .in16(1'b0), .in17(1'b0), .in18(1'b0), .in19(1'b0), .in20(1'b0), .in21(1'b0), .in22(1'b0), .in23(1'b0),
    .in24(1'b0), .in25(1'b0), .in26(1'b0), .in27(1'b0), .in28(1'b0), .in29(1'b0), .in30(1'b0), .in31(1'b0),
    .out(RegWEn5), .sel(WriteIndex));
  Multiplexer #(.select(5)) multiplexer_14 (
    .in0(1'b0), .in1(1'b0), .in2(1'b0), .in3(1'b0), .in4(1'b0), .in5(1'b0), .in6(RegWEn), .in7(1'b0),
    .in8(1'b0), .in9(1'b0), .in10(1'b0), .in11(1'b0), .in12(1'b0), .in13(1'b0), .in14(1'b0), .in15(1'b0),
    .in16(1'b0), .in17(1'b0), .in18(1'b0), .in19(1'b0), .in20(1'b0), .in21(1'b0), .in22(1'b0), .in23(1'b0),
    .in24(1'b0), .in25(1'b0), .in26(1'b0), .in27(1'b0), .in28(1'b0), .in29(1'b0), .in30(1'b0), .in31(1'b0),
    .out(RegWEn6), .sel(WriteIndex));
  Multiplexer #(.select(5)) multiplexer_15 (
    .in0(1'b0), .in1(1'b0), .in2(1'b0), .in3(1'b0), .in4(1'b0), .in5(1'b0), .in6(1'b0), .in7(RegWEn),
    .in8(1'b0), .in9(1'b0), .in10(1'b0), .in11(1'b0), .in12(1'b0), .in13(1'b0), .in14(1'b0), .in15(1'b0),
    .in16(1'b0), .in17(1'b0), .in18(1'b0), .in19(1'b0), .in20(1'b0), .in21(1'b0), .in22(1'b0), .in23(1'b0),
    .in24(1'b0), .in25(1'b0), .in26(1'b0), .in27(1'b0), .in28(1'b0), .in29(1'b0), .in30(1'b0), .in31(1'b0),
    .out(RegWEn7), .sel(WriteIndex));
  Multiplexer #(.select(5)) multiplexer_16 (
    .in0(1'b0), .in1(1'b0), .in2(1'b0), .in3(1'b0), .in4(1'b0), .in5(1'b0), .in6(1'b0), .in7(1'b0),
    .in8(RegWEn), .in9(1'b0), .in10(1'b0), .in11(1'b0), .in12(1'b0), .in13(1'b0), .in14(1'b0), .in15(1'b0),
    .in16(1'b0), .in17(1'b0), .in18(1'b0), .in19(1'b0), .in20(1'b0), .in21(1'b0), .in22(1'b0), .in23(1'b0),
    .in24(1'b0), .in25(1'b0), .in26(1'b0), .in27(1'b0), .in28(1'b0), .in29(1'b0), .in30(1'b0), .in31(1'b0),
    .out(RegWEn8), .sel(WriteIndex));
  Register #(.width(32)) register_1 (.D({32{1'b0}}), .en(RegWEn), .clk(clk), .Q(zero));  // open: clr
  Register #(.width(32)) register_2 (.D(data1), .en(RegWEn1), .clk(clk), .Q(ra));  // open: clr
  Register #(.width(32)) register_3 (.D(data2), .en(RegWEn2), .clk(clk), .Q(sp));  // open: clr
  Register #(.width(32)) register_4 (.D(data3), .en(RegWEn3), .clk(clk), .Q(gp));  // open: clr
  Register #(.width(32)) register_5 (.D(data4), .en(RegWEn4), .clk(clk), .Q(tp));  // open: clr
  Register #(.width(32)) register_6 (.D(data5), .en(RegWEn5), .clk(clk), .Q(t0));  // open: clr
  Register #(.width(32)) register_7 (.D(data6), .en(RegWEn6), .clk(clk), .Q(t1));  // open: clr
  Register #(.width(32)) register_8 (.D(data7), .en(RegWEn7), .clk(clk), .Q(t2));  // open: clr
  Register #(.width(32)) register_9 (.D(data8), .en(RegWEn8), .clk(clk), .Q(s0));  // open: clr
  Register #(.width(32)) register_10 (.D(data9), .en(RegWEn9), .clk(clk), .Q(s1));  // open: clr
  Multiplexer #(.select(5)) multiplexer_17 (
    .in0(1'b0), .in1(1'b0), .in2(1'b0), .in3(1'b0), .in4(1'b0), .in5(1'b0), .in6(1'b0), .in7(1'b0),
    .in8(1'b0), .in9(RegWEn), .in10(1'b0), .in11(1'b0), .in12(1'b0), .in13(1'b0), .in14(1'b0), .in15(1'b0),
    .in16(1'b0), .in17(1'b0), .in18(1'b0), .in19(1'b0), .in20(1'b0), .in21(1'b0), .in22(1'b0), .in23(1'b0),
    .in24(1'b0), .in25(1'b0), .in26(1'b0), .in27(1'b0), .in28(1'b0), .in29(1'b0), .in30(1'b0), .in31(1'b0),
    .out(RegWEn9), .sel(WriteIndex));
  Multiplexer #(.select(5)) multiplexer_18 (
    .in0(1'b0), .in1(1'b0), .in2(1'b0), .in3(1'b0), .in4(1'b0), .in5(1'b0), .in6(1'b0), .in7(1'b0),
    .in8(1'b0), .in9(1'b0), .in10(RegWEn), .in11(1'b0), .in12(1'b0), .in13(1'b0), .in14(1'b0), .in15(1'b0),
    .in16(1'b0), .in17(1'b0), .in18(1'b0), .in19(1'b0), .in20(1'b0), .in21(1'b0), .in22(1'b0), .in23(1'b0),
    .in24(1'b0), .in25(1'b0), .in26(1'b0), .in27(1'b0), .in28(1'b0), .in29(1'b0), .in30(1'b0), .in31(1'b0),
    .out(RegWEn10), .sel(WriteIndex));
  Multiplexer #(.select(5), .width(32)) multiplexer_19 (
    .in0(zero), .in1(ra), .in2(sp), .in3(gp), .in4(tp), .in5(t0), .in6(t1), .in7(t2), .in8(s0), .in9(s1),
    .in10(a0), .in11(a1), .in12(a2), .in13(a3), .in14(a4), .in15(a5), .in16(a6), .in17(a7), .in18(s2),
    .in19(s3), .in20(s4), .in21(s5), .in22(s6), .in23(s7), .in24(s8), .in25(s9), .in26(s10), .in27(s11),
    .in28(t3), .in29(t4), .in30(t5), .in31(t6), .out(ReadData1), .sel(ReadIndex1));
  Multiplexer #(.select(5), .width(32)) multiplexer_20 (
    .in0(zero), .in1(ra), .in2(sp), .in3(gp), .in4(tp), .in5(t0), .in6(t1), .in7(t2), .in8(s0), .in9(s1),
    .in10(a0), .in11(a1), .in12(a2), .in13(a3), .in14(a4), .in15(a5), .in16(a6), .in17(a7), .in18(s2),
    .in19(s3), .in20(s4), .in21(s5), .in22(s6), .in23(s7), .in24(s8), .in25(s9), .in26(s10), .in27(s11),
    .in28(t3), .in29(t4), .in30(t5), .in31(t6), .out(ReadData2), .sel(ReadIndex2));
  Multiplexer #(.select(5), .width(32)) multiplexer_21 (
    .in9(WriteData), .out(data9), .sel(WriteIndex));  // open: in0, in1, in2, in3, in4, in5, in6, in7, in8, in10, in11, in12, in13, in14, in15, in16, in17, in18, in19, in20, in21, in22, in23, in24, in25, in26, in27, in28, in29, in30, in31
  Multiplexer #(.select(5), .width(32)) multiplexer_22 (
    .in10(WriteData), .out(data10), .sel(WriteIndex));  // open: in0, in1, in2, in3, in4, in5, in6, in7, in8, in9, in11, in12, in13, in14, in15, in16, in17, in18, in19, in20, in21, in22, in23, in24, in25, in26, in27, in28, in29, in30, in31
  Multiplexer #(.select(5), .width(32)) multiplexer_23 (
    .in11(WriteData), .out(data11), .sel(WriteIndex));  // open: in0, in1, in2, in3, in4, in5, in6, in7, in8, in9, in10, in12, in13, in14, in15, in16, in17, in18, in19, in20, in21, in22, in23, in24, in25, in26, in27, in28, in29, in30, in31
  Multiplexer #(.select(5), .width(32)) multiplexer_24 (
    .in12(WriteData), .out(data12), .sel(WriteIndex));  // open: in0, in1, in2, in3, in4, in5, in6, in7, in8, in9, in10, in11, in13, in14, in15, in16, in17, in18, in19, in20, in21, in22, in23, in24, in25, in26, in27, in28, in29, in30, in31
  Multiplexer #(.select(5), .width(32)) multiplexer_25 (
    .in13(WriteData), .out(data13), .sel(WriteIndex));  // open: in0, in1, in2, in3, in4, in5, in6, in7, in8, in9, in10, in11, in12, in14, in15, in16, in17, in18, in19, in20, in21, in22, in23, in24, in25, in26, in27, in28, in29, in30, in31
  Multiplexer #(.select(5), .width(32)) multiplexer_26 (
    .in14(WriteData), .out(data14), .sel(WriteIndex));  // open: in0, in1, in2, in3, in4, in5, in6, in7, in8, in9, in10, in11, in12, in13, in15, in16, in17, in18, in19, in20, in21, in22, in23, in24, in25, in26, in27, in28, in29, in30, in31
  Multiplexer #(.select(5), .width(32)) multiplexer_27 (
    .in15(WriteData), .out(data15), .sel(WriteIndex));  // open: in0, in1, in2, in3, in4, in5, in6, in7, in8, in9, in10, in11, in12, in13, in14, in16, in17, in18, in19, in20, in21, in22, in23, in24, in25, in26, in27, in28, in29, in30, in31
  Multiplexer #(.select(5), .width(32)) multiplexer_28 (
    .in16(WriteData), .out(data16), .sel(WriteIndex));  // open: in0, in1, in2, in3, in4, in5, in6, in7, in8, in9, in10, in11, in12, in13, in14, in15, in17, in18, in19, in20, in21, in22, in23, in24, in25, in26, in27, in28, in29, in30, in31
  Multiplexer #(.select(5)) multiplexer_29 (
    .in0(1'b0), .in1(1'b0), .in2(1'b0), .in3(1'b0), .in4(1'b0), .in5(1'b0), .in6(1'b0), .in7(1'b0),
    .in8(1'b0), .in9(1'b0), .in10(1'b0), .in11(RegWEn), .in12(1'b0), .in13(1'b0), .in14(1'b0), .in15(1'b0),
    .in16(1'b0), .in17(1'b0), .in18(1'b0), .in19(1'b0), .in20(1'b0), .in21(1'b0), .in22(1'b0), .in23(1'b0),
    .in24(1'b0), .in25(1'b0), .in26(1'b0), .in27(1'b0), .in28(1'b0), .in29(1'b0), .in30(1'b0), .in31(1'b0),
    .out(RegWEn11), .sel(WriteIndex));
  Multiplexer #(.select(5)) multiplexer_30 (
    .in0(1'b0), .in1(1'b0), .in2(1'b0), .in3(1'b0), .in4(1'b0), .in5(1'b0), .in6(1'b0), .in7(1'b0),
    .in8(1'b0), .in9(1'b0), .in10(1'b0), .in11(1'b0), .in12(RegWEn), .in13(1'b0), .in14(1'b0), .in15(1'b0),
    .in16(1'b0), .in17(1'b0), .in18(1'b0), .in19(1'b0), .in20(1'b0), .in21(1'b0), .in22(1'b0), .in23(1'b0),
    .in24(1'b0), .in25(1'b0), .in26(1'b0), .in27(1'b0), .in28(1'b0), .in29(1'b0), .in30(1'b0), .in31(1'b0),
    .out(RegWEn12), .sel(WriteIndex));
  Register #(.width(32)) register_11 (.D(data10), .en(RegWEn10), .clk(clk), .Q(a0));  // open: clr
  Register #(.width(32)) register_12 (.D(data11), .en(RegWEn11), .clk(clk), .Q(a1));  // open: clr
  Register #(.width(32)) register_13 (.D(data12), .en(RegWEn12), .clk(clk), .Q(a2));  // open: clr
  Register #(.width(32)) register_14 (.D(data13), .en(RegWEn13), .clk(clk), .Q(a3));  // open: clr
  Register #(.width(32)) register_15 (.D(data14), .en(RegWEn14), .clk(clk), .Q(a4));  // open: clr
  Register #(.width(32)) register_16 (.D(data15), .en(RegWEn15), .clk(clk), .Q(a5));  // open: clr
  Register #(.width(32)) register_17 (.D(data16), .en(RegWEn16), .clk(clk), .Q(a6));  // open: clr
  Register #(.width(32)) register_18 (.D(data17), .en(RegWEn17), .clk(clk), .Q(a7));  // open: clr
  Register #(.width(32)) register_19 (.D(data18), .en(RegWEn18), .clk(clk), .Q(s2));  // open: clr
  Register #(.width(32)) register_20 (.D(data19), .en(RegWEn19), .clk(clk), .Q(s3));  // open: clr
  Multiplexer #(.select(5)) multiplexer_31 (
    .in0(1'b0), .in1(1'b0), .in2(1'b0), .in3(1'b0), .in4(1'b0), .in5(1'b0), .in6(1'b0), .in7(1'b0),
    .in8(1'b0), .in9(1'b0), .in10(1'b0), .in11(1'b0), .in12(1'b0), .in13(RegWEn), .in14(1'b0), .in15(1'b0),
    .in16(1'b0), .in17(1'b0), .in18(1'b0), .in19(1'b0), .in20(1'b0), .in21(1'b0), .in22(1'b0), .in23(1'b0),
    .in24(1'b0), .in25(1'b0), .in26(1'b0), .in27(1'b0), .in28(1'b0), .in29(1'b0), .in30(1'b0), .in31(1'b0),
    .out(RegWEn13), .sel(WriteIndex));
  Multiplexer #(.select(5)) multiplexer_32 (
    .in0(1'b0), .in1(1'b0), .in2(1'b0), .in3(1'b0), .in4(1'b0), .in5(1'b0), .in6(1'b0), .in7(1'b0),
    .in8(1'b0), .in9(1'b0), .in10(1'b0), .in11(1'b0), .in12(1'b0), .in13(1'b0), .in14(RegWEn), .in15(1'b0),
    .in16(1'b0), .in17(1'b0), .in18(1'b0), .in19(1'b0), .in20(1'b0), .in21(1'b0), .in22(1'b0), .in23(1'b0),
    .in24(1'b0), .in25(1'b0), .in26(1'b0), .in27(1'b0), .in28(1'b0), .in29(1'b0), .in30(1'b0), .in31(1'b0),
    .out(RegWEn14), .sel(WriteIndex));
  Multiplexer #(.select(5)) multiplexer_33 (
    .in0(1'b0), .in1(1'b0), .in2(1'b0), .in3(1'b0), .in4(1'b0), .in5(1'b0), .in6(1'b0), .in7(1'b0),
    .in8(1'b0), .in9(1'b0), .in10(1'b0), .in11(1'b0), .in12(1'b0), .in13(1'b0), .in14(1'b0), .in15(RegWEn),
    .in16(1'b0), .in17(1'b0), .in18(1'b0), .in19(1'b0), .in20(1'b0), .in21(1'b0), .in22(1'b0), .in23(1'b0),
    .in24(1'b0), .in25(1'b0), .in26(1'b0), .in27(1'b0), .in28(1'b0), .in29(1'b0), .in30(1'b0), .in31(1'b0),
    .out(RegWEn15), .sel(WriteIndex));
  Multiplexer #(.select(5)) multiplexer_34 (
    .in0(1'b0), .in1(1'b0), .in2(1'b0), .in3(1'b0), .in4(1'b0), .in5(1'b0), .in6(1'b0), .in7(1'b0),
    .in8(1'b0), .in9(1'b0), .in10(1'b0), .in11(1'b0), .in12(1'b0), .in13(1'b0), .in14(1'b0), .in15(1'b0),
    .in16(RegWEn), .in17(1'b0), .in18(1'b0), .in19(1'b0), .in20(1'b0), .in21(1'b0), .in22(1'b0), .in23(1'b0),
    .in24(1'b0), .in25(1'b0), .in26(1'b0), .in27(1'b0), .in28(1'b0), .in29(1'b0), .in30(1'b0), .in31(1'b0),
    .out(RegWEn16), .sel(WriteIndex));
  Register #(.width(32)) register_21 (.D(data20), .en(RegWEn20), .clk(clk), .Q(s4));  // open: clr
  Register #(.width(32)) register_22 (.D(data21), .en(RegWEn21), .clk(clk), .Q(s5));  // open: clr
  Register #(.width(32)) register_23 (.D(data22), .en(RegWEn22), .clk(clk), .Q(s6));  // open: clr
  Register #(.width(32)) register_24 (.D(data23), .en(RegWEn23), .clk(clk), .Q(s7));  // open: clr
  Register #(.width(32)) register_25 (.D(data24), .en(RegWEn24), .clk(clk), .Q(s8));  // open: clr
  Register #(.width(32)) register_26 (.D(data25), .en(RegWEn25), .clk(clk), .Q(s9));  // open: clr
  Register #(.width(32)) register_27 (.D(data26), .en(RegWEn26), .clk(clk), .Q(s10));  // open: clr
  Register #(.width(32)) register_28 (.D(data27), .en(RegWEn27), .clk(clk), .Q(s11));  // open: clr
  Register #(.width(32)) register_29 (.D(data28), .en(RegWEn28), .clk(clk), .Q(t3));  // open: clr
  Register #(.width(32)) register_30 (.D(data29), .en(RegWEn29), .clk(clk), .Q(t4));  // open: clr
  Multiplexer #(.select(5), .width(32)) multiplexer_35 (
    .in17(WriteData), .out(data17), .sel(WriteIndex));  // open: in0, in1, in2, in3, in4, in5, in6, in7, in8, in9, in10, in11, in12, in13, in14, in15, in16, in18, in19, in20, in21, in22, in23, in24, in25, in26, in27, in28, in29, in30, in31
  Multiplexer #(.select(5), .width(32)) multiplexer_36 (
    .in18(WriteData), .out(data18), .sel(WriteIndex));  // open: in0, in1, in2, in3, in4, in5, in6, in7, in8, in9, in10, in11, in12, in13, in14, in15, in16, in17, in19, in20, in21, in22, in23, in24, in25, in26, in27, in28, in29, in30, in31
  Multiplexer #(.select(5), .width(32)) multiplexer_37 (
    .in19(WriteData), .out(data19), .sel(WriteIndex));  // open: in0, in1, in2, in3, in4, in5, in6, in7, in8, in9, in10, in11, in12, in13, in14, in15, in16, in17, in18, in20, in21, in22, in23, in24, in25, in26, in27, in28, in29, in30, in31
  Multiplexer #(.select(5), .width(32)) multiplexer_38 (
    .in20(WriteData), .out(data20), .sel(WriteIndex));  // open: in0, in1, in2, in3, in4, in5, in6, in7, in8, in9, in10, in11, in12, in13, in14, in15, in16, in17, in18, in19, in21, in22, in23, in24, in25, in26, in27, in28, in29, in30, in31
  Multiplexer #(.select(5), .width(32)) multiplexer_39 (
    .in21(WriteData), .out(data21), .sel(WriteIndex));  // open: in0, in1, in2, in3, in4, in5, in6, in7, in8, in9, in10, in11, in12, in13, in14, in15, in16, in17, in18, in19, in20, in22, in23, in24, in25, in26, in27, in28, in29, in30, in31
  Multiplexer #(.select(5), .width(32)) multiplexer_40 (
    .in22(WriteData), .out(data22), .sel(WriteIndex));  // open: in0, in1, in2, in3, in4, in5, in6, in7, in8, in9, in10, in11, in12, in13, in14, in15, in16, in17, in18, in19, in20, in21, in23, in24, in25, in26, in27, in28, in29, in30, in31
  Multiplexer #(.select(5), .width(32)) multiplexer_41 (
    .in23(WriteData), .out(data23), .sel(WriteIndex));  // open: in0, in1, in2, in3, in4, in5, in6, in7, in8, in9, in10, in11, in12, in13, in14, in15, in16, in17, in18, in19, in20, in21, in22, in24, in25, in26, in27, in28, in29, in30, in31
  Multiplexer #(.select(5), .width(32)) multiplexer_42 (
    .in24(WriteData), .out(data24), .sel(WriteIndex));  // open: in0, in1, in2, in3, in4, in5, in6, in7, in8, in9, in10, in11, in12, in13, in14, in15, in16, in17, in18, in19, in20, in21, in22, in23, in25, in26, in27, in28, in29, in30, in31
  Register #(.width(32)) register_31 (.D(data30), .en(RegWEn30), .clk(clk), .Q(t5));  // open: clr
  Register #(.width(32)) register_32 (.D(data31), .en(RegWEn31), .clk(clk), .Q(t6));  // open: clr
  Multiplexer #(.select(5)) multiplexer_43 (
    .in0(1'b0), .in1(1'b0), .in2(1'b0), .in3(1'b0), .in4(1'b0), .in5(1'b0), .in6(1'b0), .in7(1'b0),
    .in8(1'b0), .in9(1'b0), .in10(1'b0), .in11(1'b0), .in12(1'b0), .in13(1'b0), .in14(1'b0), .in15(1'b0),
    .in16(1'b0), .in17(RegWEn), .in18(1'b0), .in19(1'b0), .in20(1'b0), .in21(1'b0), .in22(1'b0), .in23(1'b0),
    .in24(1'b0), .in25(1'b0), .in26(1'b0), .in27(1'b0), .in28(1'b0), .in29(1'b0), .in30(1'b0), .in31(1'b0),
    .out(RegWEn17), .sel(WriteIndex));
  Multiplexer #(.select(5)) multiplexer_44 (
    .in0(1'b0), .in1(1'b0), .in2(1'b0), .in3(1'b0), .in4(1'b0), .in5(1'b0), .in6(1'b0), .in7(1'b0),
    .in8(1'b0), .in9(1'b0), .in10(1'b0), .in11(1'b0), .in12(1'b0), .in13(1'b0), .in14(1'b0), .in15(1'b0),
    .in16(1'b0), .in17(1'b0), .in18(RegWEn), .in19(1'b0), .in20(1'b0), .in21(1'b0), .in22(1'b0), .in23(1'b0),
    .in24(1'b0), .in25(1'b0), .in26(1'b0), .in27(1'b0), .in28(1'b0), .in29(1'b0), .in30(1'b0), .in31(1'b0),
    .out(RegWEn18), .sel(WriteIndex));
  Multiplexer #(.select(5)) multiplexer_45 (
    .in0(1'b0), .in1(1'b0), .in2(1'b0), .in3(1'b0), .in4(1'b0), .in5(1'b0), .in6(1'b0), .in7(1'b0),
    .in8(1'b0), .in9(1'b0), .in10(1'b0), .in11(1'b0), .in12(1'b0), .in13(1'b0), .in14(1'b0), .in15(1'b0),
    .in16(1'b0), .in17(1'b0), .in18(1'b0), .in19(RegWEn), .in20(1'b0), .in21(1'b0), .in22(1'b0), .in23(1'b0),
    .in24(1'b0), .in25(1'b0), .in26(1'b0), .in27(1'b0), .in28(1'b0), .in29(1'b0), .in30(1'b0), .in31(1'b0),
    .out(RegWEn19), .sel(WriteIndex));
  Multiplexer #(.select(5)) multiplexer_46 (
    .in0(1'b0), .in1(1'b0), .in2(1'b0), .in3(1'b0), .in4(1'b0), .in5(1'b0), .in6(1'b0), .in7(1'b0),
    .in8(1'b0), .in9(1'b0), .in10(1'b0), .in11(1'b0), .in12(1'b0), .in13(1'b0), .in14(1'b0), .in15(1'b0),
    .in16(1'b0), .in17(1'b0), .in18(1'b0), .in19(1'b0), .in20(RegWEn), .in21(1'b0), .in22(1'b0), .in23(1'b0),
    .in24(1'b0), .in25(1'b0), .in26(1'b0), .in27(1'b0), .in28(1'b0), .in29(1'b0), .in30(1'b0), .in31(1'b0),
    .out(RegWEn20), .sel(WriteIndex));
  Multiplexer #(.select(5)) multiplexer_47 (
    .in0(1'b0), .in1(1'b0), .in2(1'b0), .in3(1'b0), .in4(1'b0), .in5(1'b0), .in6(1'b0), .in7(1'b0),
    .in8(1'b0), .in9(1'b0), .in10(1'b0), .in11(1'b0), .in12(1'b0), .in13(1'b0), .in14(1'b0), .in15(1'b0),
    .in16(1'b0), .in17(1'b0), .in18(1'b0), .in19(1'b0), .in20(1'b0), .in21(RegWEn), .in22(1'b0), .in23(1'b0),
    .in24(1'b0), .in25(1'b0), .in26(1'b0), .in27(1'b0), .in28(1'b0), .in29(1'b0), .in30(1'b0), .in31(1'b0),
    .out(RegWEn21), .sel(WriteIndex));
  Multiplexer #(.select(5)) multiplexer_48 (
    .in0(1'b0), .in1(1'b0), .in2(1'b0), .in3(1'b0), .in4(1'b0), .in5(1'b0), .in6(1'b0), .in7(1'b0),
    .in8(1'b0), .in9(1'b0), .in10(1'b0), .in11(1'b0), .in12(1'b0), .in13(1'b0), .in14(1'b0), .in15(1'b0),
    .in16(1'b0), .in17(1'b0), .in18(1'b0), .in19(1'b0), .in20(1'b0), .in21(1'b0), .in22(RegWEn), .in23(1'b0),
    .in24(1'b0), .in25(1'b0), .in26(1'b0), .in27(1'b0), .in28(1'b0), .in29(1'b0), .in30(1'b0), .in31(1'b0),
    .out(RegWEn22), .sel(WriteIndex));
  Multiplexer #(.select(5)) multiplexer_49 (
    .in0(1'b0), .in1(1'b0), .in2(1'b0), .in3(1'b0), .in4(1'b0), .in5(1'b0), .in6(1'b0), .in7(1'b0),
    .in8(1'b0), .in9(1'b0), .in10(1'b0), .in11(1'b0), .in12(1'b0), .in13(1'b0), .in14(1'b0), .in15(1'b0),
    .in16(1'b0), .in17(1'b0), .in18(1'b0), .in19(1'b0), .in20(1'b0), .in21(1'b0), .in22(1'b0), .in23(RegWEn),
    .in24(1'b0), .in25(1'b0), .in26(1'b0), .in27(1'b0), .in28(1'b0), .in29(1'b0), .in30(1'b0), .in31(1'b0),
    .out(RegWEn23), .sel(WriteIndex));
  Multiplexer #(.select(5)) multiplexer_50 (
    .in0(1'b0), .in1(1'b0), .in2(1'b0), .in3(1'b0), .in4(1'b0), .in5(1'b0), .in6(1'b0), .in7(1'b0),
    .in8(1'b0), .in9(1'b0), .in10(1'b0), .in11(1'b0), .in12(1'b0), .in13(1'b0), .in14(1'b0), .in15(1'b0),
    .in16(1'b0), .in17(1'b0), .in18(1'b0), .in19(1'b0), .in20(1'b0), .in21(1'b0), .in22(1'b0), .in23(1'b0),
    .in24(RegWEn), .in25(1'b0), .in26(1'b0), .in27(1'b0), .in28(1'b0), .in29(1'b0), .in30(1'b0), .in31(1'b0),
    .out(RegWEn24), .sel(WriteIndex));
  Multiplexer #(.select(5), .width(32)) multiplexer_51 (
    .in25(WriteData), .out(data25), .sel(WriteIndex));  // open: in0, in1, in2, in3, in4, in5, in6, in7, in8, in9, in10, in11, in12, in13, in14, in15, in16, in17, in18, in19, in20, in21, in22, in23, in24, in26, in27, in28, in29, in30, in31
  Multiplexer #(.select(5), .width(32)) multiplexer_52 (
    .in26(WriteData), .out(data26), .sel(WriteIndex));  // open: in0, in1, in2, in3, in4, in5, in6, in7, in8, in9, in10, in11, in12, in13, in14, in15, in16, in17, in18, in19, in20, in21, in22, in23, in24, in25, in27, in28, in29, in30, in31
  Multiplexer #(.select(5), .width(32)) multiplexer_53 (
    .in27(WriteData), .out(data27), .sel(WriteIndex));  // open: in0, in1, in2, in3, in4, in5, in6, in7, in8, in9, in10, in11, in12, in13, in14, in15, in16, in17, in18, in19, in20, in21, in22, in23, in24, in25, in26, in28, in29, in30, in31
  Multiplexer #(.select(5), .width(32)) multiplexer_54 (
    .in28(WriteData), .out(data28), .sel(WriteIndex));  // open: in0, in1, in2, in3, in4, in5, in6, in7, in8, in9, in10, in11, in12, in13, in14, in15, in16, in17, in18, in19, in20, in21, in22, in23, in24, in25, in26, in27, in29, in30, in31
  Multiplexer #(.select(5), .width(32)) multiplexer_55 (
    .in29(WriteData), .out(data29), .sel(WriteIndex));  // open: in0, in1, in2, in3, in4, in5, in6, in7, in8, in9, in10, in11, in12, in13, in14, in15, in16, in17, in18, in19, in20, in21, in22, in23, in24, in25, in26, in27, in28, in30, in31
  Multiplexer #(.select(5), .width(32)) multiplexer_56 (
    .in30(WriteData), .out(data30), .sel(WriteIndex));  // open: in0, in1, in2, in3, in4, in5, in6, in7, in8, in9, in10, in11, in12, in13, in14, in15, in16, in17, in18, in19, in20, in21, in22, in23, in24, in25, in26, in27, in28, in29, in31
  Multiplexer #(.select(5), .width(32)) multiplexer_57 (
    .in31(WriteData), .out(data31), .sel(WriteIndex));  // open: in0, in1, in2, in3, in4, in5, in6, in7, in8, in9, in10, in11, in12, in13, in14, in15, in16, in17, in18, in19, in20, in21, in22, in23, in24, in25, in26, in27, in28, in29, in30
  Multiplexer #(.select(5)) multiplexer_58 (
    .in0(1'b0), .in1(1'b0), .in2(1'b0), .in3(1'b0), .in4(1'b0), .in5(1'b0), .in6(1'b0), .in7(1'b0),
    .in8(1'b0), .in9(1'b0), .in10(1'b0), .in11(1'b0), .in12(1'b0), .in13(1'b0), .in14(1'b0), .in15(1'b0),
    .in16(1'b0), .in17(1'b0), .in18(1'b0), .in19(1'b0), .in20(1'b0), .in21(1'b0), .in22(1'b0), .in23(1'b0),
    .in24(1'b0), .in25(RegWEn), .in26(1'b0), .in27(1'b0), .in28(1'b0), .in29(1'b0), .in30(1'b0), .in31(1'b0),
    .out(RegWEn25), .sel(WriteIndex));
  Multiplexer #(.select(5)) multiplexer_59 (
    .in0(1'b0), .in1(1'b0), .in2(1'b0), .in3(1'b0), .in4(1'b0), .in5(1'b0), .in6(1'b0), .in7(1'b0),
    .in8(1'b0), .in9(1'b0), .in10(1'b0), .in11(1'b0), .in12(1'b0), .in13(1'b0), .in14(1'b0), .in15(1'b0),
    .in16(1'b0), .in17(1'b0), .in18(1'b0), .in19(1'b0), .in20(1'b0), .in21(1'b0), .in22(1'b0), .in23(1'b0),
    .in24(1'b0), .in25(1'b0), .in26(RegWEn), .in27(1'b0), .in28(1'b0), .in29(1'b0), .in30(1'b0), .in31(1'b0),
    .out(RegWEn26), .sel(WriteIndex));
  Multiplexer #(.select(5)) multiplexer_60 (
    .in0(1'b0), .in1(1'b0), .in2(1'b0), .in3(1'b0), .in4(1'b0), .in5(1'b0), .in6(1'b0), .in7(1'b0),
    .in8(1'b0), .in9(1'b0), .in10(1'b0), .in11(1'b0), .in12(1'b0), .in13(1'b0), .in14(1'b0), .in15(1'b0),
    .in16(1'b0), .in17(1'b0), .in18(1'b0), .in19(1'b0), .in20(1'b0), .in21(1'b0), .in22(1'b0), .in23(1'b0),
    .in24(1'b0), .in25(1'b0), .in26(1'b0), .in27(RegWEn), .in28(1'b0), .in29(1'b0), .in30(1'b0), .in31(1'b0),
    .out(RegWEn27), .sel(WriteIndex));
  Multiplexer #(.select(5)) multiplexer_61 (
    .in0(1'b0), .in1(1'b0), .in2(1'b0), .in3(1'b0), .in4(1'b0), .in5(1'b0), .in6(1'b0), .in7(1'b0),
    .in8(1'b0), .in9(1'b0), .in10(1'b0), .in11(1'b0), .in12(1'b0), .in13(1'b0), .in14(1'b0), .in15(1'b0),
    .in16(1'b0), .in17(1'b0), .in18(1'b0), .in19(1'b0), .in20(1'b0), .in21(1'b0), .in22(1'b0), .in23(1'b0),
    .in24(1'b0), .in25(1'b0), .in26(1'b0), .in27(1'b0), .in28(RegWEn), .in29(1'b0), .in30(1'b0), .in31(1'b0),
    .out(RegWEn28), .sel(WriteIndex));
  Multiplexer #(.select(5)) multiplexer_62 (
    .in0(1'b0), .in1(1'b0), .in2(1'b0), .in3(1'b0), .in4(1'b0), .in5(1'b0), .in6(1'b0), .in7(1'b0),
    .in8(1'b0), .in9(1'b0), .in10(1'b0), .in11(1'b0), .in12(1'b0), .in13(1'b0), .in14(1'b0), .in15(1'b0),
    .in16(1'b0), .in17(1'b0), .in18(1'b0), .in19(1'b0), .in20(1'b0), .in21(1'b0), .in22(1'b0), .in23(1'b0),
    .in24(1'b0), .in25(1'b0), .in26(1'b0), .in27(1'b0), .in28(1'b0), .in29(RegWEn), .in30(1'b0), .in31(1'b0),
    .out(RegWEn29), .sel(WriteIndex));
  Multiplexer #(.select(5)) multiplexer_63 (
    .in0(1'b0), .in1(1'b0), .in2(1'b0), .in3(1'b0), .in4(1'b0), .in5(1'b0), .in6(1'b0), .in7(1'b0),
    .in8(1'b0), .in9(1'b0), .in10(1'b0), .in11(1'b0), .in12(1'b0), .in13(1'b0), .in14(1'b0), .in15(1'b0),
    .in16(1'b0), .in17(1'b0), .in18(1'b0), .in19(1'b0), .in20(1'b0), .in21(1'b0), .in22(1'b0), .in23(1'b0),
    .in24(1'b0), .in25(1'b0), .in26(1'b0), .in27(1'b0), .in28(1'b0), .in29(1'b0), .in30(RegWEn), .in31(1'b0),
    .out(RegWEn30), .sel(WriteIndex));
  Multiplexer #(.select(5)) multiplexer_64 (
    .in0(1'b0), .in1(1'b0), .in2(1'b0), .in3(1'b0), .in4(1'b0), .in5(1'b0), .in6(1'b0), .in7(1'b0),
    .in8(1'b0), .in9(1'b0), .in10(1'b0), .in11(1'b0), .in12(1'b0), .in13(1'b0), .in14(1'b0), .in15(1'b0),
    .in16(1'b0), .in17(1'b0), .in18(1'b0), .in19(1'b0), .in20(1'b0), .in21(1'b0), .in22(1'b0), .in23(1'b0),
    .in24(1'b0), .in25(1'b0), .in26(1'b0), .in27(1'b0), .in28(1'b0), .in29(1'b0), .in30(1'b0), .in31(RegWEn),
    .out(RegWEn31), .sel(WriteIndex));

  // Notes on the sheet:
  //   INPUTS to your circuit
  //   DON'T CHANGE THE LOCATIONS OF THE INPUTS AND OUTPUTS!
  //   These are DEBUG/TEST outputs from your circuit.
  //   OUTPUTS from your circuit
endmodule
