// Logisim project test_custom.circ as structural Verilog: 1 circuit, main circuit run_main
module run_main (
  output [31:0] ra,
  output [31:0] sp,
  output [31:0] t0,
  output [31:0] t1,
  output [31:0] t2,
  output [31:0] s0,
  output [31:0] s1,
  output [31:0] a0,
  output [31:0] RequestedAddress,
  output [31:0] RequestedInstruction,
  output [15:0] TimeStep,
  output halt
);

  wire clk;

  Clock clock_1 (.out(clk));
  // Probe on RequestedAddress
  // cpu_harness cpu_harness_1: pin names not known; wires that end beside it: RequestedInstruction, clk, RequestedAddress, ra, sp, t0, t1, t2, s0, s1, a0
  ROM #(.addrWidth(14), .dataWidth(32)) rom_1 (.addr(RequestedAddress[15:2]), .data(RequestedInstruction));
  // Probe on RequestedInstruction
  Counter #(.max('hffff), .width(16)) counter_1 (.clk(clk), .Q(TimeStep));  // open: clr, load, up, count, D, carry
  Comparator #(.width(16)) comparator_1 (.a(TimeStep), .b(16'h43), .eq(halt));  // open: gt, lt

  // Other names for the same wires on the sheet: Instruction[31:0] = RequestedInstruction;
  //   ProgramCounter[31:0] = RequestedAddress

  // Notes on the sheet:
  //   contents of rom_1 (hex, n*v repeats v):
  //   300293 ffe00293 4012d313 500293 4022d313 1b00293 32f313 42e313 52c313 329313 22d313 ff900293 32d313
  //   32a313 ffd2a313 ff72a313 900293 32a313 c2a313 ff300413 7fb00493 1700913 ff100293 300393 728333
  //   f00293 300393 728333 4072d333 40745333 72f333 72e333 72c333 729333 72d333 745333 72a333 53a333
  //   542333 82a333 40538333 40740333 40828333 2728333 2828333 3248333 2848333 2728333 2828333 3248333
  //   2848333 2728333 2828333 3248333 2848333 c800413 16440493 4942823 5042283 5041283 5241303 5040283
  //   5140303 5240383 5340283
  //   Instruction Memory
  //   Halts Execution After Constant # of Clock Cycles
  //   Constant
endmodule
